// Logisim project parm.circ as structural Verilog: 21 circuits, main circuit main
module LogicalLeftShifter (
  input  [31:0] B,
  input  [4:0] Shift,
  output [31:0] S,
  output CarryOut
);

  wire [4:0] subtractor_1_out;

  Shifter #(.width(32)) shifter_1 (.in(B), .\dist (Shift), .out(S));
  BitSelector #(.width(32)) bitselector_1 (.in(B), .out(CarryOut), .sel(subtractor_1_out));
  Subtractor #(.width(5)) subtractor_1 (.a({5{1'b0}}), .b(Shift), .out(subtractor_1_out));  // open: bin, bout
endmodule

module LogicalRightShifter (
  input  [31:0] B,
  input  [4:0] Shift,
  output [31:0] S,
  output CarryOut
);

  wire [4:0] subtractor_1_out;

  Shifter #(.width(32), .shift("lr")) shifter_1 (.in(B), .\dist (Shift), .out(S));
  BitSelector #(.width(32)) bitselector_1 (.in(B), .out(CarryOut), .sel(subtractor_1_out));
  Subtractor #(.width(5)) subtractor_1 (.a(Shift), .b(5'b00001), .out(subtractor_1_out));  // open: bin, bout
endmodule

module ArithmeticRightShifter (
  input  [31:0] B,
  input  [4:0] Shift,
  output [31:0] S,
  output CarryOut
);

  wire [4:0] subtractor_1_out;

  Shifter #(.width(32), .shift("ar")) shifter_1 (.in(B), .\dist (Shift), .out(S));
  BitSelector #(.width(32)) bitselector_1 (.in(B), .out(CarryOut), .sel(subtractor_1_out));
  Subtractor #(.width(5)) subtractor_1 (.a(Shift), .b(5'b00001), .out(subtractor_1_out));  // open: bin, bout
endmodule

module RotationRightShifter (
  input  [31:0] B,
  input  [4:0] Shift,
  output [31:0] S,
  output CarryOut
);

  Shifter #(.width(32), .shift("rr")) shifter_1 (.in(B), .\dist (Shift), .out({CarryOut, S[30:0]}));

  assign S[31] = CarryOut;
endmodule

module AdderCircuit (
  input  CarryIn,
  input  [31:0] A,
  input  [31:0] B,
  output [31:0] S,
  output CarryOut,
  output Overflow
);

  wire and_1_out, and_2_out;

  Adder #(.width(32)) adder_1 (.a(A), .b(B), .out(S), .cin(CarryIn), .cout(CarryOut));
  and and_1 (and_1_out, S[31], ~B[31], ~A[31]);  // AND_Gate
  and and_2 (and_2_out, ~S[31], B[31], A[31]);  // AND_Gate
  or or_1 (Overflow, and_1_out, and_2_out);
endmodule

module SubtractorCircuit (
  input  CarryIn,
  input  [31:0] A,
  input  [31:0] B,
  output [31:0] S,
  output CarryOut,
  output Overflow
);

  wire and_1_out, and_2_out;

  Subtractor #(.width(32)) subtractor_1 (.a(A), .b(B), .out(S), .bin(CarryIn), .bout(CarryOut));
  and and_1 (and_1_out, ~S[31], ~B[31], A[31]);  // AND_Gate
  and and_2 (and_2_out, S[31], B[31], ~A[31]);  // AND_Gate
  or or_1 (Overflow, and_1_out, and_2_out);
endmodule

module MultiplierCircuit (
  input  [31:0] A,
  input  [31:0] B,
  output [31:0] S
);

  Multiplier #(.width(32)) multiplier_1 (.a(A), .b(B), .out(S));  // open: cin, cout
endmodule

module ArithmeticLogicUnit (
  input  [31:0] A,
  input  [31:0] B,
  input  [4:0] Shift,
  input  [3:0] Opcode,
  input  CarryIn,
  output [31:0] S,
  output [3:0] Flags
);

  wire ADC_C, ADC_V, ASR_C, CMN_C, CMN_V, CMP_C, CMP_V, LSL_C, LSR_C, not_1_out, ROR_C, SBC_C, SBC_V;
  wire [30:0] S_t;
  wire [31:0] ADC_S, AND_S, ASR_S, BIC_S, CMN_S, CMP_S, EOR_S, LSL_S, LSR_S, MUL_S, MVN_S, ORR_S, ROR_S,
       RSB_S, SBC_S, TST_S;

  assign AND_S = A & B;  // AND_Gate and_1, 32 bits wide
  assign EOR_S = A ^ B;  // XOR_Gate xor_1, 32 bits wide
  LogicalLeftShifter logicalleftshifter_1 (.Shift(Shift), .B(B), .S(LSL_S), .CarryOut(LSL_C));
  LogicalRightShifter logicalrightshifter_1 (.Shift(Shift), .B(B), .S(LSR_S), .CarryOut(LSR_C));
  ArithmeticRightShifter arithmeticrightshifter_1 (.B(B), .Shift(Shift), .S(ASR_S), .CarryOut(ASR_C));
  AdderCircuit addercircuit_1 (.A(A), .B(B), .CarryIn(CarryIn), .Overflow(ADC_V), .S(ADC_S), .CarryOut(ADC_C));
  not not_1 (not_1_out, CarryIn);
  SubtractorCircuit subtractorcircuit_1 (
    .Overflow(SBC_V), .A(B), .CarryIn(not_1_out), .B(A), .S(SBC_S), .CarryOut(SBC_C));
  RotationRightShifter rotationrightshifter_1 (.B(B), .S(ROR_S), .Shift(Shift), .CarryOut(ROR_C));
  assign TST_S = A & B;  // AND_Gate and_2, 32 bits wide
  SubtractorCircuit subtractorcircuit_2 (.A({32{1'b0}}), .CarryIn(1'b0), .B(A), .S(RSB_S));  // open: Overflow, CarryOut
  SubtractorCircuit subtractorcircuit_3 (.Overflow(CMP_V), .A(B), .CarryIn(1'b0), .B(A), .S(CMP_S), .CarryOut(CMP_C));
  AdderCircuit addercircuit_2 (.A(A), .B(B), .CarryIn(1'b0), .Overflow(CMN_V), .S(CMN_S), .CarryOut(CMN_C));
  assign ORR_S = A | B;  // OR_Gate or_1, 32 bits wide
  MultiplierCircuit multipliercircuit_1 (.S(MUL_S), .B(B), .A(A));
  assign BIC_S = A & ~B;  // AND_Gate and_3, 32 bits wide
  assign MVN_S = ~A;  // NOT_Gate not_2, 32 bits wide
  Multiplexer #(.select(4), .width(32), .enable("false")) multiplexer_1 (
    .in0(AND_S), .in1(EOR_S), .in2(LSL_S), .in3(LSR_S), .in4(ASR_S), .in5(ADC_S), .in6(SBC_S), .in7(ROR_S),
    .in8(TST_S), .in9(RSB_S), .in10(CMP_S), .in11(CMN_S), .in12(ORR_S), .in13(MUL_S), .in14(BIC_S),
    .in15(MVN_S), .out({Flags[3], S_t}), .sel(Opcode));
  Multiplexer #(.select(4), .enable("false")) multiplexer_2 (
    .in0(1'b0), .in1(1'b0), .in2(LSL_C), .in3(LSR_C), .in4(ASR_C), .in5(ADC_C), .in6(SBC_C), .in7(ROR_C),
    .in8(1'b0), .in9(1'b0), .in10(CMP_C), .in11(CMN_C), .in12(1'b0), .in13(1'b0), .in14(1'b0), .in15(1'b0),
    .out(Flags[1]), .sel(Opcode));
  Multiplexer #(.select(4), .enable("false")) multiplexer_3 (
    .in0(1'b0), .in1(1'b0), .in2(1'b0), .in3(1'b0), .in4(1'b0), .in5(ADC_V), .in6(SBC_V), .in7(1'b0),
    .in8(1'b0), .in9(1'b0), .in10(CMP_V), .in11(CMN_V), .in12(1'b0), .in13(1'b0), .in14(1'b0), .in15(1'b0),
    .out(Flags[0]), .sel(Opcode));
  Multiplexer #(.select(4), .width(32), .enable("false")) multiplexer_4 (
    .in0({Flags[3], S_t}), .in1({Flags[3], S_t}), .in2({Flags[3], S_t}), .in3({Flags[3], S_t}),
    .in4({Flags[3], S_t}), .in5({Flags[3], S_t}), .in6({Flags[3], S_t}), .in7({Flags[3], S_t}), .in8(B),
    .in9({Flags[3], S_t}), .in10(B), .in11(B), .in12({Flags[3], S_t}), .in13({Flags[3], S_t}),
    .in14({Flags[3], S_t}), .in15({Flags[3], S_t}), .out(S), .sel(Opcode));
  Comparator #(.width(32)) comparator_1 (.a({Flags[3], S_t}), .b({32{1'b0}}), .eq(Flags[2]));  // open: gt, lt

  // Other names for the same wires on the sheet: Overflow = Flags[0]; CarryOut = Flags[1]; S_t[31] = Flags[3]
endmodule

module RegisterFile (
  input  [31:0] DataIn,
  input  [2:0] RegA,
  input  [2:0] RegB,
  input  [2:0] RegDest,
  input  Reset,
  input  Clk,
  output [31:0] A,
  output [31:0] B,
  output [31:0] R0,
  output [31:0] R1,
  output [31:0] R2,
  output [31:0] R3,
  output [31:0] R4,
  output [31:0] R5,
  output [31:0] R6,
  output [31:0] R7
);

  wire R0_Enable, R1_Enable, R2_Enable, R3_Enable, R4_Enable, R5_Enable, R6_Enable, R7_Enable;

  Decoder #(.select(3)) decoder_1 (
    .out0(R0_Enable), .out1(R1_Enable), .out2(R2_Enable), .out3(R3_Enable), .out4(R4_Enable),
    .out5(R5_Enable), .out6(R6_Enable), .out7(R7_Enable), .sel(RegDest), .en(1'b1));
  Register #(.width(32)) register_1 (.D(DataIn), .en(R0_Enable), .clk(Clk), .Q(R0), .clr(Reset));
  Register #(.width(32)) register_2 (.D(DataIn), .en(R1_Enable), .clk(Clk), .Q(R1), .clr(Reset));
  Register #(.width(32)) register_3 (.D(DataIn), .en(R2_Enable), .clk(Clk), .Q(R2), .clr(Reset));
  Register #(.width(32)) register_4 (.D(DataIn), .en(R3_Enable), .clk(Clk), .Q(R3), .clr(Reset));
  Register #(.width(32)) register_5 (.D(DataIn), .en(R4_Enable), .clk(Clk), .Q(R4), .clr(Reset));
  Register #(.width(32)) register_6 (.D(DataIn), .en(R5_Enable), .clk(Clk), .Q(R5), .clr(Reset));
  Register #(.width(32)) register_7 (.D(DataIn), .en(R6_Enable), .clk(Clk), .Q(R6), .clr(Reset));
  Register #(.width(32)) register_8 (.D(DataIn), .en(R7_Enable), .clk(Clk), .Q(R7), .clr(Reset));
  Multiplexer #(.select(3), .width(32), .enable("false")) multiplexer_1 (
    .in0(R0), .in1(R1), .in2(R2), .in3(R3), .in4(R4), .in5(R5), .in6(R6), .in7(R7), .out(A), .sel(RegA));
  Multiplexer #(.select(3), .width(32), .enable("false")) multiplexer_2 (
    .in0(R0), .in1(R1), .in2(R2), .in3(R3), .in4(R4), .in5(R5), .in6(R6), .in7(R7), .out(B), .sel(RegB));
endmodule

module InstructionDecoder (
  input  [5:0] Opcode,
  output Shift,
  output DataProcessing,
  output LoadStore,
  output StackPointer,
  output Branch
);

  and and_1 (Shift, ~Opcode[5], ~Opcode[4]);  // AND_Gate
  and and_2 (DataProcessing, ~Opcode[5], Opcode[4], ~Opcode[3], ~Opcode[2], ~Opcode[1], ~Opcode[0]);  // AND_Gate
  and and_3 (LoadStore, Opcode[5], ~Opcode[4], ~Opcode[3], Opcode[2]);  // AND_Gate
  and and_4 (StackPointer, Opcode[5], ~Opcode[4], Opcode[3], Opcode[2]);  // AND_Gate
  and and_5 (Branch, Opcode[5], Opcode[4], ~Opcode[3], Opcode[2]);  // AND_Gate
endmodule

module Shift (
  input  [15:0] Instruction,
  input  Enable,
  output Carry,
  output [2:0] Rm,
  output [2:0] Rn,
  output [2:0] Rd,
  output [3:0] Opcode,
  output [3:0] Flags_Update_Mask,
  output [4:0] Imm5,
  output Imm32_Enable,
  output [31:0] Imm32
);

  wire multiplexer_2_out, multiplexer_5_out, multiplexer_6_out, multiplexer_13_out;
  wire [2:0] multiplexer_3_out, multiplexer_7_out, multiplexer_8_out, multiplexer_9_out;
  wire [3:0] multiplexer_4_out, multiplexer_10_out, multiplexer_11_out;
  wire [4:0] multiplexer_12_out;
  wire [31:0] bit_extender_1_out, bit_extender_2_out, multiplexer_1_out, multiplexer_14_out, subtractor_1_out;

  assign bit_extender_1_out = {{29{1'b0}}, Instruction[8:6]};  // Bit_Extender bit_extender_1
  assign bit_extender_2_out = {{24{1'b0}}, Instruction[7:0]};  // Bit_Extender bit_extender_2
  Multiplexer #(.select(2), .width(32), .enable("false")) multiplexer_1 (
    .in0({32{1'b0}}), .in1({32{1'b0}}), .in2(bit_extender_1_out), .in3(bit_extender_1_out),
    .out(multiplexer_1_out), .sel(Instruction[10:9]));
  Subtractor #(.width(32)) subtractor_1 (
    .a({32{1'b0}}), .b(bit_extender_2_out), .out(subtractor_1_out), .bin(1'b0));  // open: bout
  Multiplexer #(.select(2), .enable("false")) multiplexer_2 (
    .in0(1'b0), .in1(1'b1), .in2(1'b0), .in3(1'b1), .out(multiplexer_2_out), .sel(Instruction[10:9]));
  Multiplexer #(.select(2), .width(3), .enable("false")) multiplexer_3 (
    .in0(Instruction[8:6]), .in1(Instruction[8:6]), .in2(3'b000), .in3(3'b000), .out(multiplexer_3_out),
    .sel(Instruction[10:9]));
  Multiplexer #(.select(2), .width(4), .enable("false")) multiplexer_4 (
    .in0(4'b0101), .in1(4'b0110), .in2(4'b0101), .in3(4'b0110), .out(multiplexer_4_out),
    .sel(Instruction[10:9]));
  Multiplexer #(.select(2), .enable("false")) multiplexer_5 (
    .in0(1'b0), .in1(1'b0), .in2(1'b1), .in3(1'b1), .out(multiplexer_5_out), .sel(Instruction[10:9]));
  Multiplexer #(.select(3), .enable("false")) multiplexer_6 (
    .in0(1'b0), .in1(1'b0), .in2(1'b0), .in3(multiplexer_2_out), .in4(1'b0), .in5(1'b0), .in6(1'b0),
    .in7(1'b0), .out(multiplexer_6_out), .sel(Instruction[13:11]));
  Multiplexer #(.select(3), .width(3), .enable("false")) multiplexer_7 (
    .in0(3'b000), .in1(3'b000), .in2(3'b000), .in3(multiplexer_3_out), .in4(3'b000), .in5(3'b000),
    .in6(3'b000), .in7(3'b000), .out(multiplexer_7_out), .sel(Instruction[13:11]));
  Multiplexer #(.select(3), .width(3), .enable("false")) multiplexer_8 (
    .in0(Instruction[5:3]), .in1(Instruction[5:3]), .in2(Instruction[5:3]), .in3(Instruction[5:3]),
    .in4(3'b000), .in5(3'b000), .in6(3'b000), .in7(3'b000), .out(multiplexer_8_out), .sel(Instruction[13:11]));
  Multiplexer #(.select(3), .width(3), .enable("false")) multiplexer_9 (
    .in0(Instruction[2:0]), .in1(Instruction[2:0]), .in2(Instruction[2:0]), .in3(Instruction[2:0]),
    .in4(Instruction[10:8]), .in5(3'b000), .in6(3'b000), .in7(3'b000), .out(multiplexer_9_out),
    .sel(Instruction[13:11]));
  Multiplexer #(.select(3), .width(4), .enable("false")) multiplexer_10 (
    .in0(4'b0010), .in1(4'b0011), .in2(4'b0100), .in3(multiplexer_4_out), .in4(4'b1001), .in5(4'b0000),
    .in6(4'b0000), .in7(4'b0000), .out(multiplexer_10_out), .sel(Instruction[13:11]));
  Multiplexer #(.select(3), .width(4), .enable("false")) multiplexer_11 (
    .in0(4'b1110), .in1(4'b1110), .in2(4'b1110), .in3(4'b1111), .in4(4'b1100), .in5(4'b0000), .in6(4'b0000),
    .in7(4'b0000), .out(multiplexer_11_out), .sel(Instruction[13:11]));
  Multiplexer #(.select(3), .width(5), .enable("false")) multiplexer_12 (
    .in0(Instruction[10:6]), .in1(Instruction[10:6]), .in2(Instruction[10:6]), .in3({5{1'b0}}),
    .in4({5{1'b0}}), .in5({5{1'b0}}), .in6({5{1'b0}}), .in7({5{1'b0}}), .out(multiplexer_12_out),
    .sel(Instruction[13:11]));
  Multiplexer #(.select(3), .enable("false")) multiplexer_13 (
    .in0(1'b0), .in1(1'b0), .in2(1'b0), .in3(multiplexer_5_out), .in4(1'b1), .in5(1'b0), .in6(1'b0),
    .in7(1'b0), .out(multiplexer_13_out), .sel(Instruction[13:11]));
  Multiplexer #(.select(3), .width(32), .enable("false")) multiplexer_14 (
    .in0({32{1'b0}}), .in1({32{1'b0}}), .in2({32{1'b0}}), .in3(multiplexer_1_out), .in4(subtractor_1_out),
    .in5({32{1'b0}}), .in6({32{1'b0}}), .in7({32{1'b0}}), .out(multiplexer_14_out), .sel(Instruction[13:11]));
  Multiplexer #(.enable("false")) multiplexer_15 (.in0(1'b0), .in1(multiplexer_6_out), .out(Carry), .sel(Enable));
  Multiplexer #(.width(3), .enable("false")) multiplexer_16 (
    .in0(3'b000), .in1(multiplexer_7_out), .out(Rm), .sel(Enable));
  Multiplexer #(.width(3), .enable("false")) multiplexer_17 (
    .in0(3'b000), .in1(multiplexer_8_out), .out(Rn), .sel(Enable));
  Multiplexer #(.width(3), .enable("false")) multiplexer_18 (
    .in0(3'b000), .in1(multiplexer_9_out), .out(Rd), .sel(Enable));
  Multiplexer #(.width(4), .enable("false")) multiplexer_19 (
    .in0(4'b0000), .in1(multiplexer_10_out), .out(Opcode), .sel(Enable));
  Multiplexer #(.width(4), .enable("false")) multiplexer_20 (
    .in0(4'b0000), .in1(multiplexer_11_out), .out(Flags_Update_Mask), .sel(Enable));
  Multiplexer #(.width(5), .enable("false")) multiplexer_21 (
    .in0({5{1'b0}}), .in1(multiplexer_12_out), .out(Imm5), .sel(Enable));
  Multiplexer #(.enable("false")) multiplexer_22 (
    .in0(1'b0), .in1(multiplexer_13_out), .out(Imm32_Enable), .sel(Enable));
  Multiplexer #(.width(32), .enable("false")) multiplexer_23 (
    .in0({32{1'b0}}), .in1(multiplexer_14_out), .out(Imm32), .sel(Enable));

  // Other names for the same wires on the sheet: Imm8[7:0] = Instruction[7:0]; Rd_t[2:0] = Instruction[2:0];
  //   Rn_t[2:0] = Instruction[5:3]; Imm3[2:0] = Instruction[8:6]; Imm5_t[4:0] = Instruction[10:6];
  //   Rm_t[2:0] = Instruction[8:6]; Rd_bis[2:0] = Instruction[10:8]; AddSub[1:0] = Instruction[10:9];
  //   Opcode_t[2:0] = Instruction[13:11]
endmodule

module DataProcessing (
  input  [15:0] Instruction,
  input  Enable,
  output [2:0] Rm,
  output [2:0] Rn,
  output [2:0] Rd,
  output [3:0] Opcode,
  output [3:0] Flags_Update_Mask
);

  wire [3:0] multiplexer_1_out;

  Multiplexer #(.select(4), .width(4), .enable("false")) multiplexer_1 (
    .in0(4'b1110), .in1(4'b1110), .in2(4'b1110), .in3(4'b1110), .in4(4'b1110), .in5(4'b1111), .in6(4'b1111),
    .in7(4'b1110), .in8(4'b1110), .in9(4'b1111), .in10(4'b1111), .in11(4'b1111), .in12(4'b1110),
    .in13(4'b1100), .in14(4'b1110), .in15(4'b1110), .out(multiplexer_1_out), .sel(Instruction[9:6]));
  Multiplexer #(.width(3), .enable("false")) multiplexer_2 (
    .in0(3'b000), .in1(Instruction[5:3]), .out(Rm), .sel(Enable));
  Multiplexer #(.width(3), .enable("false")) multiplexer_3 (
    .in0(3'b000), .in1(Instruction[2:0]), .out(Rd), .sel(Enable));
  Multiplexer #(.width(4), .enable("false")) multiplexer_4 (
    .in0(4'b0000), .in1(Instruction[9:6]), .out(Opcode), .sel(Enable));
  Multiplexer #(.width(4), .enable("false")) multiplexer_5 (
    .in0(4'b0000), .in1(multiplexer_1_out), .out(Flags_Update_Mask), .sel(Enable));

  assign Rn = Rd;

  // Other names for the same wires on the sheet: Rdn[2:0] = Instruction[2:0]; Rm_t[2:0] = Instruction[5:3];
  //   Opcode_t[3:0] = Instruction[9:6]
endmodule

module LoadStore (
  input  [15:0] Instruction,
  input  Enable,
  input  [31:0] StackPointer,
  input  Clk,
  input  Reset,
  output Load,
  output Store,
  output PC_Hold,
  output [2:0] Rm,
  output [2:0] Rd,
  output [31:0] RAM_Addr
);

  wire and_1_out, and_2_out, not_1_out, PC_Hold_t;
  wire [31:0] adder_1_out, bit_extender_1_out;

  D_Flip_Flop d_ff_1 (.D(and_1_out), .clk(Clk), .Qn(PC_Hold_t), .preset(1'b0), .reset(Reset));  // open: Q
  and and_1 (and_1_out, PC_Hold_t, Enable);
  assign bit_extender_1_out = {{24{Instruction[7]}}, Instruction[7:0]};  // Bit_Extender bit_extender_1
  Adder #(.width(32)) adder_1 (.a(StackPointer), .b(bit_extender_1_out), .out(adder_1_out));  // open: cin, cout
  and and_2 (and_2_out, Instruction[11], ~PC_Hold_t);  // AND_Gate
  Multiplexer #(.width(3), .enable("false")) multiplexer_1 (
    .in0(3'b000), .in1(Instruction[10:8]), .out(Rd), .sel(Enable));
  Multiplexer #(.enable("false")) multiplexer_2 (.in0(1'b0), .in1(and_2_out), .out(Load), .sel(Enable));
  Multiplexer #(.enable("false")) multiplexer_3 (.in0(1'b0), .in1(not_1_out), .out(Store), .sel(Enable));
  not not_1 (not_1_out, Instruction[11]);
  Multiplexer #(.enable("false")) multiplexer_4 (.in0(1'b0), .in1(PC_Hold_t), .out(PC_Hold), .sel(Enable));
  Multiplexer #(.width(32), .enable("false")) multiplexer_5 (
    .in0({32{1'b0}}), .in1(adder_1_out), .out(RAM_Addr), .sel(Enable));

  assign Rm = Rd;

  // Other names for the same wires on the sheet: Imm8[7:0] = Instruction[7:0]; Rt[2:0] = Instruction[10:8];
  //   Load_t = Instruction[11]
endmodule

module StackPointer (
  input  [15:0] Instruction,
  input  Enable,
  input  [31:0] StackPointer,
  output Write_Enable,
  output [31:0] New_StackPointer
);

  wire [31:0] adder_1_out, bit_extender_1_out, bit_extender_2_out, multiplexer_1_out, subtractor_1_out;

  assign bit_extender_1_out = {{25{1'b0}}, Instruction[6:0]};  // Bit_Extender bit_extender_1
  assign bit_extender_2_out = {{25{1'b0}}, Instruction[6:0]};  // Bit_Extender bit_extender_2
  Adder #(.width(32)) adder_1 (.a(StackPointer), .b(bit_extender_1_out), .out(adder_1_out));  // open: cin, cout
  Subtractor #(.width(32)) subtractor_1 (
    .a(StackPointer), .b(bit_extender_2_out), .out(subtractor_1_out));  // open: bin, bout
  Multiplexer #(.width(32), .enable("false")) multiplexer_1 (
    .in0(adder_1_out), .in1(subtractor_1_out), .out(multiplexer_1_out), .sel(Instruction[7]));
  Multiplexer #(.width(32), .enable("false")) multiplexer_2 (
    .in0({32{1'b0}}), .in1(multiplexer_1_out), .out(New_StackPointer), .sel(Enable));

  assign Write_Enable = Enable;

  // Other names for the same wires on the sheet: Imm7[6:0] = Instruction[6:0]; Opcode = Instruction[7]
endmodule

module Branch (
  input  [15:0] Instruction,
  input  Enable,
  input  [3:0] Flags,
  output Verified,
  output [7:0] Offset
);

  wire CC, GE, GT, HI, LE, LS, LT, NE, PL, VC, Verified_t, xnor_2_out, xor_2_out;

  not not_1 (NE, Flags[2]);
  not not_2 (CC, Flags[1]);
  not not_3 (PL, Flags[3]);
  not not_4 (VC, Flags[0]);
  and and_1 (HI, Flags[1], ~Flags[2]);  // AND_Gate
  or or_1 (LS, ~Flags[1], Flags[2]);  // OR_Gate
  xnor xnor_1 (GE, Flags[3], Flags[0]);
  xor xor_1 (LT, Flags[3], Flags[0]);
  and and_2 (GT, ~Flags[2], xnor_2_out);  // AND_Gate
  xnor xnor_2 (xnor_2_out, Flags[3], Flags[0]);
  or or_2 (LE, Flags[2], xor_2_out);
  xor xor_2 (xor_2_out, Flags[3], Flags[0]);
  Multiplexer #(.select(4), .enable("false")) multiplexer_1 (
    .in0(Flags[2]), .in1(NE), .in2(Flags[1]), .in3(CC), .in4(Flags[3]), .in5(PL), .in6(Flags[0]), .in7(VC),
    .in8(HI), .in9(LS), .in10(GE), .in11(LT), .in12(GT), .in13(LE), .in14(1'b1), .in15(1'b0),
    .out(Verified_t), .sel(Instruction[11:8]));
  Multiplexer #(.enable("false")) multiplexer_2 (.in0(1'b0), .in1(Verified_t), .out(Verified), .sel(Enable));
  Multiplexer #(.width(8), .enable("false")) multiplexer_3 (
    .in0({8{1'b0}}), .in1(Instruction[7:0]), .out(Offset), .sel(Enable));

  // Other names for the same wires on the sheet: V = Flags[0]; VS = Flags[0]; C = Flags[1]; CS = Flags[1];
  //   EQ = Flags[2]; Z = Flags[2]; MI = Flags[3]; N = Flags[3]; Imm8[7:0] = Instruction[7:0];
  //   Opcode[3:0] = Instruction[11:8]
endmodule

module FlagsAPSR (
  input  [3:0] FlagsIn,
  input  [3:0] Flags_Update_Mask,
  input  Clk,
  input  Reset,
  output [3:0] FlagsOut
);

  wire [3:0] and_1_out, and_2_out, not_1_out, or_1_out;

  assign and_1_out = FlagsOut & not_1_out;  // AND_Gate and_1, 4 bits wide
  assign not_1_out = ~Flags_Update_Mask;  // NOT_Gate not_1, 4 bits wide
  assign and_2_out = FlagsIn & Flags_Update_Mask;  // AND_Gate and_2, 4 bits wide
  assign or_1_out = and_1_out | and_2_out;  // OR_Gate or_1, 4 bits wide
  Register #(.width(4)) register_1 (.D(or_1_out), .en(1'b1), .clk(Clk), .Q(FlagsOut), .clr(Reset));

  // Other names for the same wires on the sheet: Update_Mask[3:0] = Flags_Update_Mask
endmodule

module ProgramCounterRegister (
  input  Reset,
  input  Load,
  input  UpDown,
  input  Count,
  input  Clk,
  input  [7:0] DataIn,
  output Carry,
  output [7:0] DataOut
);

  Counter counter_1 (
    .clr(Reset), .load(Load), .up(UpDown), .count(Count), .clk(Clk), .D(DataIn), .carry(Carry), .Q(DataOut));
endmodule

module StackPointerRegister (
  input  [31:0] DataIn,
  input  Write,
  input  Clk,
  input  Reset,
  output [31:0] DataOut
);

  Register #(.width(32)) register_1 (.D(DataIn), .en(Write), .clk(Clk), .Q(DataOut), .clr(Reset));
endmodule

module ControlUnit (
  input  [15:0] Instruction,
  input  [3:0] Flags,
  input  Reset,
  input  Clk,
  output Load,
  output Store,
  output Shift_Enable,
  output Carry,
  output [2:0] Rm,
  output [2:0] Rn,
  output [2:0] Rd,
  output [3:0] Opcode,
  output [4:0] Imm5,
  output Imm32_Enable,
  output [31:0] Imm32,
  output [7:0] ROM_Address,
  output [31:0] RAM_Address,
  output [3:0] FlagsOut
);

  wire Branch_Enable, Branch_Verified, DataProcessing_Enable, LoadStore_Enable, LoadStore_PC_Hold, not_1_out,
       Shift_Carry, StackPointer_Enable, StackPointer_Write;
  wire [2:0] DataProcessing_Rd, DataProcessing_Rm, DataProcessing_Rn, LoadStore_Rd, LoadStore_Rm, Shift_Rd,
       Shift_Rm, Shift_Rn;
  wire [3:0] DataProcessing_Flags_Mask, DataProcessing_Opcode, or_1_out, Shift_Flags_Mask, Shift_Opcode;
  wire [7:0] adder_1_out, adder_2_out, Branch_Offset;
  wire [31:0] SP, StackPointer_New;

  InstructionDecoder instructiondecoder_1 (
    .StackPointer(StackPointer_Enable), .DataProcessing(DataProcessing_Enable), .LoadStore(LoadStore_Enable),
    .Shift(Shift_Enable), .Opcode(Instruction[15:10]), .Branch(Branch_Enable));
  Shift shift_1 (
    .Imm5(Imm5), .Instruction(Instruction), .Imm32(Imm32), .Carry(Shift_Carry), .Enable(Shift_Enable),
    .Imm32_Enable(Imm32_Enable), .Opcode(Shift_Opcode), .Flags_Update_Mask(Shift_Flags_Mask), .Rm(Shift_Rm),
    .Rn(Shift_Rn), .Rd(Shift_Rd));
  DataProcessing dataprocessing_1 (
    .Opcode(DataProcessing_Opcode), .Rn(DataProcessing_Rn), .Enable(DataProcessing_Enable),
    .Rm(DataProcessing_Rm), .Rd(DataProcessing_Rd), .Instruction(Instruction),
    .Flags_Update_Mask(DataProcessing_Flags_Mask));
  LoadStore loadstore_1 (
    .Reset(Reset), .Clk(Clk), .Enable(LoadStore_Enable), .Instruction(Instruction), .StackPointer(SP),
    .Load(Load), .Store(Store), .Rm(LoadStore_Rm), .Rd(LoadStore_Rd), .RAM_Addr(RAM_Address),
    .PC_Hold(LoadStore_PC_Hold));
  StackPointer stackpointer_1 (
    .New_StackPointer(StackPointer_New), .Write_Enable(StackPointer_Write), .StackPointer(SP),
    .Enable(StackPointer_Enable), .Instruction(Instruction));
  Branch branch_1 (
    .Flags(FlagsOut), .Enable(Branch_Enable), .Instruction(Instruction), .Offset(Branch_Offset),
    .Verified(Branch_Verified));
  Adder adder_1 (.a(Branch_Offset), .b(8'h3), .out(adder_1_out));  // open: cin, cout
  assign or_1_out = Shift_Flags_Mask | DataProcessing_Flags_Mask;  // OR_Gate or_1, 4 bits wide
  Adder adder_2 (.a(adder_1_out), .b(ROM_Address), .out(adder_2_out));  // open: cin, cout
  not not_1 (not_1_out, LoadStore_PC_Hold);
  StackPointerRegister stackpointerregister_1 (
    .Reset(Reset), .Write(StackPointer_Write), .Clk(Clk), .DataOut(SP), .DataIn(StackPointer_New));
  ProgramCounterRegister programcounterregister_1 (
    .Reset(Reset), .DataOut(ROM_Address), .UpDown(1'b1), .Load(Branch_Verified), .DataIn(adder_2_out),
    .Clk(Clk), .Count(not_1_out));  // open: Carry
  FlagsAPSR flagsapsr_1 (.FlagsOut(FlagsOut), .Flags_Update_Mask(or_1_out), .FlagsIn(Flags), .Reset(Reset), .Clk(Clk));
  Multiplexer #(.enable("false")) multiplexer_1 (.in0(FlagsOut[1]), .in1(Shift_Carry), .out(Carry), .sel(Shift_Enable));
  assign Rm = Shift_Rm | DataProcessing_Rm | LoadStore_Rm;  // OR_Gate or_2, 3 bits wide
  assign Rn = Shift_Rn | DataProcessing_Rn;  // OR_Gate or_3, 3 bits wide
  assign Rd = Shift_Rd | DataProcessing_Rd | LoadStore_Rd;  // OR_Gate or_4, 3 bits wide
  assign Opcode = Shift_Opcode | DataProcessing_Opcode;  // OR_Gate or_5, 4 bits wide

  // Other names for the same wires on the sheet: FlagsIn[3:0] = Flags; LoadStore_RAM_Address[31:0] = RAM_Address;
  //   PC[7:0] = ROM_Address; Shift_Imm5[4:0] = Imm5; Shift_Imm32[31:0] = Imm32; Shift_Imm32_Enable = Imm32_Enable
endmodule

module CentralProcessingUnit (
  input  [31:0] RAM_In,
  input  [15:0] ROM_In,
  input  Reset,
  input  Clk,
  output Store,
  output [7:0] ROM_Address,
  output [31:0] RAM_Address,
  output [31:0] RAM_Out,
  output [31:0] R0,
  output [31:0] R1,
  output [31:0] R2,
  output [31:0] R3,
  output [31:0] R4,
  output [31:0] R5,
  output [31:0] R6,
  output [31:0] R7,
  output [3:0] FlagsOut
);

  wire Carry, Imm32_Enable, Load, Shift_Enable;
  wire [2:0] Rd, Rm, Rn;
  wire [3:0] Flags, Opcode;
  wire [4:0] Imm5, multiplexer_4_out;
  wire [31:0] A, B, Imm32, multiplexer_1_out, multiplexer_2_out, multiplexer_3_out, S;

  ControlUnit controlunit_1 (
    .Rd(Rd), .Reset(Reset), .Shift_Enable(Shift_Enable), .Clk(Clk), .Rn(Rn), .Flags(Flags), .Carry(Carry),
    .Imm32(Imm32), .Rm(Rm), .Instruction(ROM_In), .Imm32_Enable(Imm32_Enable), .Imm5(Imm5), .Opcode(Opcode),
    .RAM_Address(RAM_Address), .Load(Load), .Store(Store), .ROM_Address(ROM_Address), .FlagsOut(FlagsOut));
  Multiplexer #(.width(32), .enable("false")) multiplexer_1 (.in0(S), .in1(A), .out(multiplexer_1_out), .sel(Store));
  Multiplexer #(.width(32), .enable("false")) multiplexer_2 (
    .in0(multiplexer_1_out), .in1(RAM_In), .out(multiplexer_2_out), .sel(Load));
  RegisterFile registerfile_1 (
    .A(A), .B(B), .RegDest(Rd), .Clk(Clk), .RegB(Rn), .RegA(Rm), .Reset(Reset), .DataIn(multiplexer_2_out),
    .R0(R0), .R1(R1), .R2(R2), .R3(R3), .R4(R4), .R5(R5), .R6(R6), .R7(R7));
  Multiplexer #(.width(32), .enable("false")) multiplexer_3 (
    .in0(A), .in1(Imm32), .out(multiplexer_3_out), .sel(Imm32_Enable));
  Multiplexer #(.width(5), .enable("false")) multiplexer_4 (
    .in0(A[4:0]), .in1(Imm5), .out(multiplexer_4_out), .sel(Shift_Enable));
  ArithmeticLogicUnit arithmeticlogicunit_1 (
    .Shift(multiplexer_4_out), .S(S), .Opcode(Opcode), .CarryIn(Carry), .A(multiplexer_3_out), .Flags(Flags),
    .B(B));
  Multiplexer #(.width(32), .enable("false")) multiplexer_5 (.in0(RAM_In), .in1(A), .out(RAM_Out), .sel(Store));
endmodule

module main (
  output [15:0] out_1,
  output [31:0] out_2,
  output [31:0] out_3,
  output [31:0] out_4,
  output [31:0] out_5,
  output [31:0] out_6,
  output [31:0] out_7,
  output [31:0] out_8,
  output [31:0] out_9,
  output [3:0] Flags__NZCV,
  output [31:0] out_11,
  output [31:0] out_12,
  output [31:0] out_13,
  output [31:0] out_14,
  output [31:0] out_15,
  output [31:0] out_16,
  output [31:0] out_17,
  output [31:0] out_18,
  output [31:0] out_19,
  output [31:0] out_20,
  output [31:0] out_21,
  output [31:0] out_22,
  output [31:0] out_23,
  output [31:0] out_24,
  output [31:0] out_25,
  output [31:0] out_26
);

  wire Clk, Reset, Store;
  wire [7:0] ROM_Address;
  wire [31:0] RAM_Address, RAM_In, RAM_Out;

  Button u_Reset (.out(Reset));
  Clock u_Clk (.out(Clk));
  CentralProcessingUnit centralprocessingunit_1 (
    .RAM_Address(RAM_Address), .RAM_In(RAM_In), .Clk(Clk), .ROM_In(out_1), .Reset(Reset),
    .ROM_Address(ROM_Address), .RAM_Out(RAM_Out), .R0(out_2), .R1(out_3), .R2(out_4), .R3(out_5),
    .R4(out_15), .R5(out_16), .R6(out_17), .R7(out_18), .Store(Store), .FlagsOut(Flags__NZCV));
  ROM #(.dataWidth(16)) rom_1 (.addr(ROM_Address), .data(out_1));
  RAM #(.dataWidth(32), .databus("bibus")) ram_1 (
    .addr(RAM_Address[7:0]), .we(Store), .oe(1'b1), .clk(Clk), .din(RAM_Out), .dout(RAM_In));

  assign out_6 = out_2;
  assign out_7 = out_3;
  assign out_8 = out_4;
  assign out_9 = out_5;
  assign out_11 = out_2;
  assign out_12 = out_3;
  assign out_13 = out_4;
  assign out_14 = out_5;
  assign out_19 = out_15;
  assign out_20 = out_16;
  assign out_21 = out_17;
  assign out_22 = out_18;
  assign out_23 = out_15;
  assign out_24 = out_16;
  assign out_25 = out_17;
  assign out_26 = out_18;

  // Other names for the same wires on the sheet: Flags[3:0] = Flags__NZCV; R0[31:0] = out_2; R1[31:0] = out_3;
  //   R2[31:0] = out_4; R3[31:0] = out_5; R4[31:0] = out_15; R5[31:0] = out_16; R6[31:0] = out_17; R7[31:0] = out_18;
  //   ROM_In[15:0] = out_1

  // Notes on the sheet:
  //   Instruction
  //   Controls
  //   Registers
  //   contents of rom_1 (hex, n*v repeats v):
  //   b084 2300 9304 2300 930c 2301 9308 9a0c 9b08 189b 9304 9b08 930c 9b04 9308 def5 defd
  //   ARM Retarded Machine
  //   Etienne BEGUIER
  //   Martin BOUTEILLER
  //   João BRILHANTE
  //   Olivier DOUSSAUD
endmodule
