// Logisim project tests.circ as structural Verilog: 2 circuits, main circuit RegisterFileTest
module RegisterFileTest (
  input  Reset,
  output Clk,
  output [31:0] A,
  output [31:0] B,
  output [31:0] R0,
  output [31:0] R1,
  output [31:0] R2,
  output [31:0] R3,
  output [31:0] R4,
  output [31:0] R5,
  output [31:0] R6,
  output [31:0] R7
);

  wire and_1_out, EndDataIn, EndRegDest, shift_register_1_p4;
  wire [2:0] RegA, RegDest;
  wire [31:0] counter_1_q, DataIn;

  Clock sysclk (.out(Clk));
  // Shift_Register #(.length(2)) shift_register_1: pin names not known; wires that end beside it: Reset, Clk, EndDataIn, shift_register_1_p4
  Counter #(.width(32), .max('h7), .ongoal("stay")) counter_1 (
    .clr(Reset), .load(1'b0), .up(1'b1), .count(1'b1), .clk(Clk), .carry(EndDataIn), .Q(counter_1_q));  // open: D
  Counter #(.width(3), .max('h7), .ongoal("stay")) counter_2 (
    .clr(Reset), .load(1'b0), .up(1'b1), .count(1'b1), .clk(Clk), .carry(EndRegDest), .Q(RegDest));  // open: D
  and and_1 (and_1_out, Clk, shift_register_1_p4);
  Counter #(.width(3), .max('h7), .ongoal("stay")) counter_3 (
    .clr(Reset), .load(1'b0), .up(1'b1), .count(1'b1), .clk(and_1_out), .Q(RegA));  // open: D, carry
  Adder #(.width(32)) adder_1 (.a(counter_1_q), .b(32'h1), .out(DataIn));  // open: cin, cout
  RegisterFile registerfile_1 (
    .A(A), .B(B), .RegDest(RegDest), .Clk(Clk), .RegB(RegA), .RegA(RegA), .Reset(Reset), .DataIn(DataIn),
    .R0(R0), .R1(R1), .R2(R2), .R3(R3), .R4(R4), .R5(R5), .R6(R6), .R7(R7));

  // Notes on the sheet:
  //   Set the registers.
  //   Read the registers.
endmodule

module FlagsAPSRTest (
  input  Reset,
  output Clk,
  output [3:0] FlagsIn,
  output [3:0] Flags_Update_Mask,
  output [3:0] FlagsOut
);

  wire d_ff_1_q, EndFlagsIn, EndFlagsMask;

  Clock sysclk (.out(Clk));
  D_Flip_Flop d_ff_1 (.D(EndFlagsIn), .clk(Clk), .Q(d_ff_1_q));  // open: Qn, preset, reset
  Counter #(.width(4), .max('hf), .ongoal("stay")) counter_1 (
    .clr(Reset), .load(1'b0), .up(1'b1), .count(1'b1), .clk(d_ff_1_q), .carry(EndFlagsMask),
    .Q(Flags_Update_Mask));  // open: D
  Counter #(.width(4), .max('hf)) counter_2 (
    .clr(Reset), .load(1'b0), .up(1'b1), .count(1'b1), .clk(Clk), .carry(EndFlagsIn), .Q(FlagsIn));  // open: D
  FlagsAPSR flagsapsr_1 (
    .FlagsOut(FlagsOut), .Flags_Update_Mask(Flags_Update_Mask), .FlagsIn(FlagsIn), .Reset(Reset), .Clk(Clk));

  // Other names for the same wires on the sheet: Flags_Mask[3:0] = Flags_Update_Mask

  // Notes on the sheet:
  //   For each flags update mask.
  //   For each flags in.
endmodule
